# Fritzing sketch analogInOutSerial_connection (saved by Fritzing 0.7.11b)
breadboards: 1

parts:
  R1 = Rotary Potentiometer (Small) [maximum_resistance=100kΩ]
  Arduino1 = Arduino
  LED1 = LED - 5mm [color="Red (633nm)" package="5 mm [THT]"]

nets:
  N1: R1.leg1, Arduino1.GND, LED1.cathode
  N2: R1.wiper, Arduino1.A0
  N3: R1.leg2, Arduino1.+5V
  N4: Arduino1.D9, LED1.anode
