# Fritzing sketch analogSensor_conn (saved by Fritzing 0.7.11b)
breadboards: 1

parts:
  Arduino1 = Arduino
  R1 = Photocell (LDR) [package=THT]
  R2 = Resistor [tolerance=±5% resistance=220 package=THT]

nets:
  N1: Arduino1.GND, R1.pin_1
  N2: Arduino1.+5V, R2.Pin_0
  N3: Arduino1.A0, R1.pin_0, R2.Pin_1
