# Fritzing sketch button_onoff (saved by Fritzing 0.7.11b)
breadboards: 1

parts:
  S1 = Pushbutton [package="[THT]"]
  Arduino1 = Arduino
  LED1 = LED - 5mm [color="Red (633nm)" package="5 mm [THT]"]
  R1 = Resistor [tolerance=±5% resistance=220 package=THT]

nets:
  N1: S1.Pin_1, S1.Pin_2, Arduino1.+5V
  N2: S1.Pin_3, S1.Pin_4, Arduino1.D2, R1.Pin_0
  N3: Arduino1.D12, LED1.anode
  N4: Arduino1.GND, LED1.cathode, R1.Pin_1
