# Fritzing sketch XbeePCB (saved by Fritzing 0.7.11b)
breadboards: 1

parts:
  J1 = Generic female header - 6 pins [package=THT]
  L2 = smd LED [color="Red (633nm)" package="0805 [SMD]"]
  Xbee = XBee
  L1 = smd LED [color="Red (633nm)" package="0805 [SMD]"]
  R1 = Resistor [tolerance=±5% resistance=220 package="0805 [SMD]"]
  R2 = Resistor [tolerance=±5% resistance=220 package="0805 [SMD]"]

nets (from the pcb view):
  N1: J1.pin1, L2.cathode, Xbee.pin9, Xbee.GND, L1.cathode
  N2: J1.pin2, Xbee.pin12
  N3: J1.pin3, Xbee.VCC, Xbee.pin16
  N4: J1.pin4, Xbee.pin2
  N5: J1.pin5, Xbee.pin3
  N6: L2.anode, R2.Pin_1
  N7: Xbee.pin13, R2.Pin_0
  N8: Xbee.pin15, R1.Pin_1
  N9: L1.anode, R1.Pin_0

notes:
  3V
  TX
  RX
  GND
