# Fritzing sketch heatcontrolling (saved by Fritzing 0.7.11b)
breadboards: 1

parts:
  Arduino1 = Arduino
  Q2 = npn-Powertransistor [part_number=TIP122 package="TO220 [THT]"]
  S1 = Round Pushbutton
  R1 = 100k Ω Resistor [package=THT]
  R2 = 100 Ω Resistor [package=THT]
  LED1 = green LED - 5mm
  L1 = Inductor [part_number="Heat element" package="400 mil [THT]"]
  VCC1 = Battery block 9V

nets:
  GND: Arduino1.GND, Q2.emitter, S1.leg0, R1.Pin_0, VCC1.-
  N1: Arduino1.D9, R2.Pin_1
  N2: Arduino1.D2, S1.leg1
  N3: Arduino1.3V3, LED1.anode
  N4: Q2.base, R1.Pin_1, R2.Pin_0
  N5: Q2.collector, LED1.cathode, L1.pin_0
  N6: L1.pin_1, VCC1.+
