# Fritzing sketch heatcontrolling2 (saved by Fritzing 0.7.11b)
breadboards: 1

parts:
  Arduino1 = Arduino
  Q2 = npn-Powertransistor [part_number=TIP122 package="TO220 [THT]"]
  S1 = Round Pushbutton
  R1 = 100k Ω Resistor [package=THT]
  R2 = 100 Ω Resistor [package=THT]
  Q3 = npn-Powertransistor [part_number=TIP122 package="TO220 [THT]"]
  R3 = 100 Ω Resistor [package=THT]
  R4 = 100k Ω Resistor [package=THT]
  LED2 = green LED - 5mm
  LED3 = green LED - 5mm
  L1 = Inductor [part_number="heat element1" package="400 mil [THT]"]
  L2 = Inductor [part_number="heat element2" package="400 mil [THT]"]
  VCC1 = Battery block 9V

nets:
  GND: Arduino1.GND, Q2.emitter, S1.leg0, R1.Pin_0, Q3.emitter, R4.Pin_0, VCC1.-
  N1: Arduino1.D9, R2.Pin_1
  N2: Arduino1.D5, R3.Pin_1
  N3: Arduino1.D2, S1.leg1
  N4: Arduino1.3V3, LED2.anode, LED3.anode
  N5: Q2.base, R1.Pin_1, R2.Pin_0
  N6: Q2.collector, LED3.cathode, L1.pin_1
  N7: Q3.base, R3.Pin_0, R4.Pin_1
  N8: Q3.collector, LED2.cathode, L2.pin_1
  N9: L1.pin_0, L2.pin_0, VCC1.+
